# Fritzing sketch 3 (saved by Fritzing 1.0.6)
breadboards: 1

parts:
  U1 = 74HC04_HEX_INVERTER [package=dil14]
  LED1 = LED - 5mm [color="Red (633nm)" current=0.030A package="5 mm [THT]"]
  R1 = Resistor [tolerance=±5% resistance=220 package="0603 [SMD]"]
  VCC1 = 4 x AAA Battery Mount [internal_resistance=0.1Ω]

nets:
  N1: U1.1A, U1.VCC, VCC1.+
  N2: U1.1Y, U1.2A
  N3: U1.2Y, U1.3A
  N4: U1.3Y, U1.4A
  N5: U1.GND, R1.Pin_0, VCC1.-
  N6: U1.4Y, U1.5A
  N7: U1.5Y, U1.6A
  N8: U1.6Y, LED1.anode
  N9: LED1.cathode, R1.Pin_1
