# Fritzing sketch 74HC04 (saved by Fritzing 1.0.6)
breadboards: 1

parts:
  U1 = 74HC04_HEX_INVERTER [package=dil14]
  VCC1 = Battery [internal_resistance=0.1Ω]
  LED1 = smd LED [color="Red (633nm)" package="1206 [SMD]"]
  R1 = Resistor [tolerance=±5% resistance=220 package="0603 [SMD]"]

nets:
  N1: U1.1A, VCC1.+
  N2: U1.1Y, U1.2A
  N3: U1.2Y, U1.3A
  N4: U1.3Y, U1.4A
  N5: U1.4Y, U1.5A
  N6: U1.5Y, U1.6A
  N7: U1.6Y, R1.Pin_1
  N8: VCC1.-, LED1.cathode
  N9: LED1.anode, R1.Pin_0
