# Fritzing sketch LED_circuit (saved by Fritzing 1.0.6)
breadboards: 1

parts:
  VCC1 = 4 x AAA Battery Mount [internal_resistance=0.1Ω]
  LED1 = smd LED [color="Red (633nm)" package="1206 [SMD]"]
  R1 = Resistor [tolerance=±5% resistance=220 package="0402 [SMD]"]

nets:
  N1: VCC1.-, LED1.cathode
  N2: VCC1.+, R1.Pin_1
  N3: LED1.anode, R1.Pin_0
