// Logisim project full_adder.circ as structural Verilog: 1 circuit, main circuit main
module main (
  input  A,
  input  B,
  input  C_in,
  output out_4,
  output out_5
);

  wire and_1_out, and_2_out, and_3_out, or_1_out, xor_1_out;

  xor xor_1 (xor_1_out, C_in, B, A);
  and and_1 (and_1_out, A, C_in);
  and and_2 (and_2_out, B, A);
  and and_3 (and_3_out, B, C_in);
  or or_1 (or_1_out, and_1_out, and_2_out, and_3_out);
endmodule
