// Logisim project ShiftRegisterInLogisim.circ as structural Verilog: 1 circuit, main circuit main
module main (
  input  Reset,
  input  Mode,
  input  Data_in,
  input  in_4,
  input  in_5,
  input  in_6,
  input  in_7
);

  wire button_1_out, not_1_out, shift_register_1_p10, shift_register_1_p11, shift_register_1_p12,
       shift_register_1_p13;

  Button button_1 (.out(button_1_out));
  not not_1 (not_1_out, Mode);
  // Shift_Register #(.length(4)) shift_register_1: pin names not known; wires that end beside it: Reset, Mode, not_1_out, button_1_out, Data_in, in_4, in_5, in_6, in_7, shift_register_1_p10, shift_register_1_p11, shift_register_1_p12, shift_register_1_p13
  // Probe on shift_register_1_p10
  // Probe on shift_register_1_p11
  // Probe on shift_register_1_p12
  // Probe on shift_register_1_p13
endmodule
