// Logisim project ShiftRegisterParLoad.circ as structural Verilog: 1 circuit, main circuit main
module main (
  input  D,
  input  C,
  input  B,
  input  A,
  input  S_in,
  input  Mode
);

  wire and_1_out, and_2_out, and_3_out, and_4_out, and_5_out, and_6_out, and_7_out, and_8_out, clock_out,
       d_ff_1_q, not_1_out, or_1_out, or_2_out, or_3_out, or_4_out, Qa, Qb, Qc;

  // Probe on d_ff_1_q
  // Probe on Qc
  // Probe on Qb
  // Probe on Qa
  Button clock (.out(clock_out));
  D_Flip_Flop d_ff_1 (.D(or_1_out), .clk(clock_out), .Q(d_ff_1_q));  // open: Qn, preset, reset
  D_Flip_Flop d_ff_2 (.D(or_2_out), .clk(clock_out), .Q(Qc));  // open: Qn, preset, reset
  D_Flip_Flop d_ff_3 (.D(or_3_out), .clk(clock_out), .Q(Qb));  // open: Qn, preset, reset
  D_Flip_Flop d_ff_4 (.D(or_4_out), .clk(clock_out), .Q(Qa));  // open: Qn, preset, reset
  or or_1 (or_1_out, and_1_out, and_2_out);
  or or_2 (or_2_out, and_3_out, and_4_out);
  or or_3 (or_3_out, and_5_out, and_6_out);
  or or_4 (or_4_out, and_7_out, and_8_out);
  and and_1 (and_1_out, D, Mode);
  and and_2 (and_2_out, Qc, not_1_out);
  and and_3 (and_3_out, C, Mode);
  and and_4 (and_4_out, Qb, not_1_out);
  and and_5 (and_5_out, B, Mode);
  and and_6 (and_6_out, Qa, not_1_out);
  and and_7 (and_7_out, A, Mode);
  and and_8 (and_8_out, not_1_out, S_in);
  not not_1 (not_1_out, Mode);
endmodule
